// Logisim project LadyBugALU.circ as structural Verilog: 2 circuits, main circuit main
module main (
  input  [15:0] B,
  input  [15:0] A,
  input  cin,
  input  [1:0] in_4,
  output out_5
);

  wire clock_1_out, not_1_out;
  wire [3:0] alu_1_r0, alu_1_r1, alu_1_r2, alu_1_r3;

  Clock clock_1 (.out(clock_1_out));
  not not_1 (not_1_out, clock_1_out);
  ALU alu_1 (
    .A(A), .B(B), .S(clock_1_out), .cin(cin), .Op(in_4), .S2(not_1_out), .CF(out_5), .R3(alu_1_r3),
    .R2(alu_1_r2), .R1(alu_1_r1), .R0(alu_1_r0));
  Hex_Digit_Display hex_digit_display_1 (.value(alu_1_r3));  // open: dp
  Hex_Digit_Display hex_digit_display_2 (.value(alu_1_r2));  // open: dp
  Hex_Digit_Display hex_digit_display_3 (.value(alu_1_r1));  // open: dp
  Hex_Digit_Display hex_digit_display_4 (.value(alu_1_r0));  // open: dp

  // Notes on the sheet:
  //   LadyBug ALU
  //   Simple 16 bits ALU, made in LadyBug Project
endmodule

module ALU (
  input  [15:0] A,
  input  [15:0] B,
  input  S,
  input  cin,
  input  [1:0] Op,
  input  S2,
  output CF,
  output [3:0] R3,
  output [3:0] R2,
  output [3:0] R1,
  output [3:0] R0
);

  wire adder_1_cout, and_2_out, and_3_out, subtractor_1_bout;
  wire [15:0] adder_1_out, and_1_out, and_4_out, and_5_out, and_6_out, and_7_out, or_1_out, or_2_out,
       register_1_q, register_2_q, subtractor_1_out;
  wire [15:15] decoder_1_out0, decoder_1_out1, decoder_1_out2, decoder_1_out3;

  Register #(.width(16)) register_1 (.D(A), .clk(S), .Q(register_1_q));  // open: en, clr
  Register #(.width(16)) register_2 (.D(B), .clk(S), .Q(register_2_q));  // open: en, clr
  Decoder #(.select(2)) decoder_1 (
    .out0(decoder_1_out0[15]), .out1(decoder_1_out1[15]), .out2(decoder_1_out2[15]),
    .out3(decoder_1_out3[15]), .sel(Op), .en(S));
  assign and_1_out = register_1_q & register_2_q;  // AND_Gate and_1, 16 bits wide
  assign or_1_out = register_1_q | register_2_q;  // OR_Gate or_1, 16 bits wide
  Adder #(.width(16)) adder_1 (.a(register_1_q), .b(register_2_q), .out(adder_1_out), .cin(cin), .cout(adder_1_cout));
  Subtractor #(.width(16)) subtractor_1 (
    .a(register_1_q), .b(register_2_q), .out(subtractor_1_out), .bin(cin), .bout(subtractor_1_bout));
  and and_2 (and_2_out, adder_1_cout, decoder_1_out2[15]);
  and and_3 (and_3_out, subtractor_1_bout, decoder_1_out3[15]);
  assign and_4_out = and_1_out & {16{decoder_1_out0[15]}};  // AND_Gate and_4, 16 bits wide
  assign and_5_out = or_1_out & {16{decoder_1_out1[15]}};  // AND_Gate and_5, 16 bits wide
  assign and_6_out = adder_1_out & {16{decoder_1_out2[15]}};  // AND_Gate and_6, 16 bits wide
  assign and_7_out = subtractor_1_out & {16{decoder_1_out3[15]}};  // AND_Gate and_7, 16 bits wide
  assign or_2_out = and_4_out | and_5_out | and_6_out | and_7_out;  // OR_Gate or_2, 16 bits wide
  or or_3 (CF, and_2_out, and_3_out);
  Register #(.width(16)) register_3 (.D(or_2_out), .clk(S2), .Q({R3, R2, R1, R0}));  // open: en, clr
endmodule
