// Logisim project LadyBugII.circ as structural Verilog: 3 circuits, main circuit main
module main (
  input  [15:0] in_1,
  input  [15:0] in_2,
  input  [1:0] in_3,
  input  in_4,
  input  [3:0] in_5,
  output out_6
);

  wire clock_1_out;
  wire [3:0] aluwmovs_1_carry_2;
  wire [11:0] aluwmovs_1_carry;
  wire [15:0] aluwmovs_1_c;

  Clock clock_1 (.out(clock_1_out));
  Hex_Digit_Display hex_digit_display_1 (.value(aluwmovs_1_carry[11:8]));  // open: dp
  Hex_Digit_Display hex_digit_display_2 (.value(aluwmovs_1_carry_2));  // open: dp
  ALUwMOVs aluwmovs_1 (
    .A(in_1), .B(in_2), .S(in_3), .clk(clock_1_out), .E(in_4), .Op(in_5), .C(aluwmovs_1_c),
    .Carry({aluwmovs_1_carry_2, aluwmovs_1_carry}), .CF(out_6));
  Hex_Digit_Display hex_digit_display_3 (.value(aluwmovs_1_carry[7:4]));  // open: dp
  Hex_Digit_Display hex_digit_display_4 (.value(aluwmovs_1_carry[3:0]));  // open: dp
  Hex_Digit_Display hex_digit_display_5 (.value(aluwmovs_1_c[15:12]));  // open: dp
  Hex_Digit_Display hex_digit_display_6 (.value(aluwmovs_1_c[11:8]));  // open: dp
  Hex_Digit_Display hex_digit_display_7 (.value(aluwmovs_1_c[7:4]));  // open: dp
  Hex_Digit_Display hex_digit_display_8 (.value(aluwmovs_1_c[3:0]));  // open: dp

  // Notes on the sheet:
  //   Carry
endmodule

module ALU (
  input  [15:0] A,
  input  [15:0] B,
  input  B0000,
  input  B0001,
  input  [1:0] s,
  input  B0010,
  input  B0011,
  input  B0100,
  input  B0101,
  input  B0110,
  input  B0111,
  input  B1000,
  input  B1001,
  input  E,
  input  [3:0] OP,
  output [15:0] C,
  output [15:0] Carry,
  output CF
);

  wire adder_1_cout, and_1_out, and_2_out, and_3_out, and_4_out, and_18_out, and_19_out, decoder_1_out0,
       decoder_1_out1, decoder_1_out2, decoder_1_out3, subtractor_1_bout;
  wire [3:0] multiplexer_1_out, multiplexer_2_out;
  wire [15:0] adder_1_out, and_5_out, and_6_out, and_7_out, and_8_out, and_9_out, and_10_out, and_11_out,
       and_12_out, and_13_out, and_14_out, and_15_out, and_16_out, and_17_out, divider_1_out, divider_1_rem,
       multiplexer_3_out, multiplexer_4_out, multiplexer_5_out, multiplexer_6_out, multiplier_1_cout,
       multiplier_1_out, negator_1_out, not_1_out, or_1_out, shifter_1_out, shifter_2_out, subtractor_1_out;

  and and_1 (and_1_out, B0111, decoder_1_out3);
  Multiplexer #(.width(4), .enable("false")) multiplexer_1 (
    .in0(B[3:0]), .in1(A[3:0]), .out(multiplexer_1_out), .sel(and_2_out));
  Multiplexer #(.width(4), .enable("false")) multiplexer_2 (
    .in0(B[3:0]), .in1(A[3:0]), .out(multiplexer_2_out), .sel(and_1_out));
  and and_2 (and_2_out, B0110, decoder_1_out2);
  and and_3 (and_3_out, B0000, decoder_1_out1);
  and and_4 (and_4_out, B0001, decoder_1_out0);
  Decoder #(.select(2), .enable("false")) decoder_1 (
    .out0(decoder_1_out0), .out1(decoder_1_out1), .out2(decoder_1_out2), .out3(decoder_1_out3), .sel(s));
  Multiplexer #(.width(16), .enable("false")) multiplexer_3 (
    .in0(A), .in1(B), .out(multiplexer_3_out), .sel(and_3_out));
  Multiplexer #(.width(16), .enable("false")) multiplexer_4 (
    .in0(A), .in1(B), .out(multiplexer_4_out), .sel(and_4_out));
  Multiplexer #(.width(16), .enable("false")) multiplexer_5 (
    .in0(A), .in1(B), .out(multiplexer_5_out), .sel(and_2_out));
  Multiplexer #(.width(16), .enable("false")) multiplexer_6 (.in0(A), .in1(B), .out(multiplexer_6_out));  // open: sel
  assign not_1_out = ~multiplexer_3_out;  // NOT_Gate not_1, 16 bits wide
  Negator #(.width(16)) negator_1 (.in(multiplexer_4_out), .out(negator_1_out));
  Adder #(.width(16)) adder_1 (.a(A), .b(B), .out(adder_1_out), .cout(adder_1_cout));  // open: cin
  Subtractor #(.width(16)) subtractor_1 (.a(A), .b(B), .out(subtractor_1_out), .bout(subtractor_1_bout));  // open: bin
  Shifter #(.width(16)) shifter_1 (.in(multiplexer_5_out), .\dist (multiplexer_1_out), .out(shifter_1_out));
  Shifter #(.width(16), .shift("lr")) shifter_2 (
    .in(multiplexer_6_out), .\dist (multiplexer_2_out), .out(shifter_2_out));
  Multiplier #(.width(16)) multiplier_1 (.a(A), .b(B), .out(multiplier_1_out), .cout(multiplier_1_cout));  // open: cin
  Divider #(.width(16)) divider_1 (.a(A), .b(B), .out(divider_1_out), .rem(divider_1_rem));  // open: upper
  assign and_5_out = A & B;  // AND_Gate and_5, 16 bits wide
  assign or_1_out = A | B;  // OR_Gate or_1, 16 bits wide
  assign and_6_out = not_1_out & {16{B0000}};  // AND_Gate and_6, 16 bits wide
  assign and_7_out = negator_1_out & {16{B0001}};  // AND_Gate and_7, 16 bits wide
  assign and_8_out = and_5_out & {16{B0010}};  // AND_Gate and_8, 16 bits wide
  assign and_9_out = or_1_out & {16{B0011}};  // AND_Gate and_9, 16 bits wide
  assign and_10_out = adder_1_out & {16{B0100}};  // AND_Gate and_10, 16 bits wide
  assign and_11_out = subtractor_1_out & {16{B0101}};  // AND_Gate and_11, 16 bits wide
  assign and_12_out = shifter_1_out & {16{B0110}};  // AND_Gate and_12, 16 bits wide
  assign and_13_out = shifter_2_out & {16{B0111}};  // AND_Gate and_13, 16 bits wide
  assign and_14_out = multiplier_1_out & {16{B1000}};  // AND_Gate and_14, 16 bits wide
  assign and_15_out = divider_1_out & {16{B1001}};  // AND_Gate and_15, 16 bits wide
  assign and_16_out = multiplier_1_cout & {16{B1000}};  // AND_Gate and_16, 16 bits wide
  assign and_17_out = {16{B1001}} & divider_1_rem;  // AND_Gate and_17, 16 bits wide
  and and_18 (and_18_out, adder_1_cout, B0100);
  and and_19 (and_19_out, subtractor_1_bout, B0101);
  assign C = and_6_out | and_7_out | and_8_out | and_9_out | and_10_out | and_11_out | and_12_out | and_13_out | and_14_out | and_15_out;  // OR_Gate or_2, 16 bits wide
  assign Carry = and_16_out | and_17_out;  // OR_Gate or_3, 16 bits wide
  or or_4 (CF, and_18_out, and_19_out);
endmodule

module ALUwMOVs (
  input  [15:0] A,
  input  [15:0] B,
  input  [1:0] S,
  input  clk,
  input  E,
  input  [3:0] Op,
  output [15:0] C,
  output [15:0] Carry,
  output CF
);

  wire decoder_1_out0, decoder_1_out1, decoder_1_out2, decoder_1_out3, decoder_1_out4, decoder_1_out5,
       decoder_1_out6, decoder_1_out7, decoder_1_out8, decoder_1_out9, decoder_1_out10, decoder_1_out11,
       decoder_1_out12, decoder_1_out13, not_1_out;
  wire [15:0] alu_1_c, alu_1_carry, multiplexer_1_out, multiplexer_2_out, multiplexer_3_out,
       multiplexer_4_out, multiplexer_5_out, multiplexer_6_out, register_1_q, register_2_q;

  Multiplexer #(.width(16), .enable("false")) multiplexer_1 (
    .in0(A), .in1(multiplexer_4_out), .out(multiplexer_1_out), .sel(decoder_1_out12));
  Register #(.width(16)) register_1 (.D(multiplexer_2_out), .clk(clk), .Q(register_1_q));  // open: en, clr
  Multiplexer #(.width(16), .enable("false")) multiplexer_2 (
    .in0(multiplexer_1_out), .in1(register_2_q), .out(multiplexer_2_out), .sel(decoder_1_out11));
  Register #(.width(16)) register_2 (.D(multiplexer_3_out), .clk(clk), .Q(register_2_q));  // open: en, clr
  Multiplexer #(.width(16), .enable("false")) multiplexer_3 (
    .in0(B), .in1(register_1_q), .out(multiplexer_3_out), .sel(decoder_1_out10));
  Multiplexer #(.width(16), .enable("false")) multiplexer_4 (
    .in0(multiplexer_5_out), .in1(multiplexer_6_out), .out(multiplexer_4_out), .sel(not_1_out));
  Multiplexer #(.width(16), .enable("false")) multiplexer_5 (
    .in0(A), .in1(C), .out(multiplexer_5_out), .sel(decoder_1_out12));
  not not_1 (not_1_out, decoder_1_out12);
  Decoder #(.select(4)) decoder_1 (
    .out0(decoder_1_out0), .out1(decoder_1_out1), .out2(decoder_1_out2), .out3(decoder_1_out3),
    .out4(decoder_1_out4), .out5(decoder_1_out5), .out6(decoder_1_out6), .out7(decoder_1_out7),
    .out8(decoder_1_out8), .out9(decoder_1_out9), .out10(decoder_1_out10), .out11(decoder_1_out11),
    .out12(decoder_1_out12), .out13(decoder_1_out13), .sel(Op), .en(E));  // open: out14, out15
  Multiplexer #(.width(16), .enable("false")) multiplexer_6 (
    .in0(A), .in1(Carry), .out(multiplexer_6_out), .sel(decoder_1_out13));
  ALU alu_1 (
    .B1001(decoder_1_out9), .B0010(decoder_1_out2), .B(register_2_q), .B0101(decoder_1_out5),
    .B0110(decoder_1_out6), .B0000(decoder_1_out0), .s(S), .B1000(decoder_1_out8), .B0011(decoder_1_out3),
    .A(register_1_q), .B0100(decoder_1_out4), .B0111(decoder_1_out7), .B0001(decoder_1_out1), .C(alu_1_c),
    .Carry(alu_1_carry), .CF(CF));  // open: E, OP
  Register #(.width(16)) register_3 (.D(alu_1_c), .clk(clk), .Q(C));  // open: en, clr
  Register #(.width(16)) register_4 (.D(alu_1_carry), .clk(clk), .Q(Carry));  // open: en, clr
endmodule
